// Logisim project Behrmann_Quinn.circ as structural Verilog: 6 circuits, main circuit auto_arm_simulation
module auto_arm_simulation (
);

  wire auto_arm_top_1_dest_blue_o, auto_arm_top_1_dest_init_o, auto_arm_top_1_dest_red_o,
       auto_arm_top_1_drop_o, auto_arm_top_1_move_o, auto_arm_top_1_scan_o, auto_arm_top_1_throw_o,
       clk_i_out, tclconsolereds_1_p23, tclconsolereds_1_p26;
  wire [1:0] tclconsolereds_1_p24;

  Clock clk_i (.out(clk_i_out));
  Clock sysclk ();  // open: out
  auto_arm_top auto_arm_top_1 (
    .ready_i(tclconsolereds_1_p23), .color_i(tclconsolereds_1_p24), .clk_i(clk_i_out),
    .reset_i(tclconsolereds_1_p26), .scan_o(auto_arm_top_1_scan_o), .throw_o(auto_arm_top_1_throw_o),
    .move_o(auto_arm_top_1_move_o), .dest_red_o(auto_arm_top_1_dest_red_o),
    .dest_blue_o(auto_arm_top_1_dest_blue_o), .dest_init_o(auto_arm_top_1_dest_init_o),
    .drop_o(auto_arm_top_1_drop_o));
  // TclConsoleReds #(.filePath("console\\console_auto_arm.tcl")) tclconsolereds_1: pin names not known; wires that end beside it: 4'b0000, 4'b0000, auto_arm_top_1_scan_o, auto_arm_top_1_throw_o, auto_arm_top_1_move_o, auto_arm_top_1_dest_red_o, auto_arm_top_1_dest_blue_o, auto_arm_top_1_dest_init_o, auto_arm_top_1_drop_o, 1'b0, 1'b0, 1'b0, 1'b0, 1'b0, 1'b0, 1'b0, 1'b0, 1'b0, {16{1'b0}}, {16{1'b0}}, {8{1'b0}}, clk_i_out, tclconsolereds_1_p23, tclconsolereds_1_p24[0], tclconsolereds_1_p24[1], tclconsolereds_1_p26

  // Notes on the sheet:
  //   Attention, votre version de Logisim
  //   ne contient pas de tracker. Si vous
  //   enregistrez votre projet, toutes les
  //   informations du tracker seront
  //   définitivement effacées.
endmodule

module auto_arm_top (
  input  ready_i,
  input  [1:0] color_i,
  input  clk_i,
  input  reset_i,
  output scan_o,
  output throw_o,
  output move_o,
  output dest_red_o,
  output dest_blue_o,
  output dest_init_o,
  output drop_o
);

  wire [6:0] decodeur_d_etats_futurs_1_etat_futur, register_7bit_1_output_o;

  Decodeur_d_etats_futurs decodeur_d_etats_futurs_1 (
    .etat_present(register_7bit_1_output_o), .ready_i(ready_i), .color_i(color_i), .clk_i(clk_i),
    .etat_futur(decodeur_d_etats_futurs_1_etat_futur));
  register_7bit register_7bit_1 (
    .input_i(decodeur_d_etats_futurs_1_etat_futur), .reset_i(reset_i), .clk_i(clk_i),
    .output_o(register_7bit_1_output_o));
  Decodeur_de_sorties decodeur_de_sorties_1 (
    .input_i(register_7bit_1_output_o),
    .output_o({scan_o, throw_o, move_o, dest_red_o, dest_blue_o, dest_init_o, drop_o}));

  // Notes on the sheet:
  //   Attention, votre version de Logisim
  //   ne contient pas de tracker. Si vous
  //   enregistrez votre projet, toutes les
  //   informations du tracker seront
  //   définitivement effacées.
endmodule

module Decodeur_de_sorties (
  input  [6:0] input_i,
  output [6:0] output_o
);

  wire [6:0] multiplexer_1_out, multiplexer_2_out, multiplexer_3_out, multiplexer_4_out, multiplexer_5_out,
       multiplexer_6_out, multiplexer_7_out;

  Multiplexer #(.width(7), .enable("false")) multiplexer_1 (
    .in0({7{1'b0}}), .in1({7{1'b0}}), .out(multiplexer_1_out), .sel(input_i[0]));
  Multiplexer #(.width(7), .enable("false")) multiplexer_2 (
    .in0({7{1'b0}}), .in1(7'b1000000), .out(multiplexer_2_out), .sel(input_i[1]));
  Multiplexer #(.width(7), .enable("false")) multiplexer_3 (
    .in0({7{1'b0}}), .in1(7'b0100000), .out(multiplexer_3_out), .sel(input_i[2]));
  Multiplexer #(.width(7), .enable("false")) multiplexer_4 (
    .in0({7{1'b0}}), .in1(7'b0010100), .out(multiplexer_4_out), .sel(input_i[3]));
  Multiplexer #(.width(7), .enable("false")) multiplexer_5 (
    .in0({7{1'b0}}), .in1(7'b0011000), .out(multiplexer_5_out), .sel(input_i[4]));
  Multiplexer #(.width(7), .enable("false")) multiplexer_6 (
    .in0({7{1'b0}}), .in1(7'b0000001), .out(multiplexer_6_out), .sel(input_i[5]));
  Multiplexer #(.width(7), .enable("false")) multiplexer_7 (
    .in0({7{1'b0}}), .in1(7'b0010010), .out(multiplexer_7_out), .sel(input_i[6]));
  assign output_o = multiplexer_1_out | multiplexer_2_out | multiplexer_3_out | multiplexer_4_out | multiplexer_5_out | multiplexer_6_out | multiplexer_7_out;  // OR_Gate or_1, 7 bits wide

  // Notes on the sheet:
  //   Attention, votre version de Logisim
  //   ne contient pas de tracker. Si vous
  //   enregistrez votre projet, toutes les
  //   informations du tracker seront
  //   définitivement effacées.
endmodule

module Decodeur_d_etats_futurs (
  input  [6:0] etat_present,
  input  ready_i,
  input  [1:0] color_i,
  input  clk_i,
  output [6:0] etat_futur
);

  wire and_1_out, and_2_out, and_3_out, and_4_out, and_5_out, and_6_out, and_7_out, and_8_out, and_10_out,
       and_11_out, and_12_out, cpmtDone, xnor_1_out;

  and and_1 (and_1_out, etat_present[1], color_i[1], ~color_i[0]);  // AND_Gate
  or or_1 (etat_futur[3], and_1_out, and_2_out);
  and and_2 (and_2_out, etat_present[3], ~cpmtDone);  // AND_Gate
  NotExactlyOne xnor_1 (.out(xnor_1_out), .in0(etat_present[4]), .in1(etat_present[6]), .in2(etat_present[3]));
  and and_3 (and_3_out, etat_present[1], ~color_i[1], color_i[0]);  // AND_Gate
  or or_2 (etat_futur[4], and_3_out, and_4_out);
  and and_4 (and_4_out, etat_present[4], ~cpmtDone);  // AND_Gate
  compteur compteur_1 (.load_i(xnor_1_out), .en_i(1'b1), .clk_i(clk_i), .reset_i(1'b0), .done_o(cpmtDone));
  and and_5 (and_5_out, etat_present[0], ~ready_i);  // AND_Gate
  or or_3 (etat_futur[0], and_5_out, etat_present[2], and_6_out);
  and and_6 (and_6_out, etat_present[6], cpmtDone);
  and and_7 (and_7_out, etat_present[0], ready_i);
  or or_4 (etat_futur[1], and_7_out, and_8_out);
  and and_8 (and_8_out, etat_present[1], color_i[1], color_i[0]);
  and and_9 (etat_futur[2], etat_present[1], ~color_i[1], ~color_i[0]);  // AND_Gate
  and and_10 (and_10_out, etat_present[4], cpmtDone);
  and and_11 (and_11_out, etat_present[3], cpmtDone);
  or or_5 (etat_futur[5], and_10_out, and_11_out);
  and and_12 (and_12_out, etat_present[6], ~cpmtDone);  // AND_Gate
  or or_6 (etat_futur[6], etat_present[5], and_12_out);

  // Other names for the same wires on the sheet: color2 = color_i[0]; color1 = color_i[1]; idleNext = etat_futur[0];
  //   scanNext = etat_futur[1]; throwNext = etat_futur[2]; moveBlueNext = etat_futur[3]; moveRedNext = etat_futur[4];
  //   dropNext = etat_futur[5]; moveInitNext = etat_futur[6]; idle = etat_present[0]; scan = etat_present[1];
  //   throw = etat_present[2]; moveBlue = etat_present[3]; moveRed = etat_present[4]; drop = etat_present[5];
  //   moveInit = etat_present[6]; ready = ready_i

  // Notes on the sheet:
  //   Attention, votre version de Logisim
  //   ne contient pas de tracker. Si vous
  //   enregistrez votre projet, toutes les
  //   informations du tracker seront
  //   définitivement effacées.
endmodule

module register_7bit (
  input  [6:0] input_i,
  input  reset_i,
  input  clk_i,
  output [6:0] output_o
);

  wire multiplexer_1_out, multiplexer_2_out, multiplexer_3_out, multiplexer_4_out, multiplexer_5_out,
       multiplexer_6_out, multiplexer_7_out, not_1_out;

  not not_1 (not_1_out, reset_i);
  Multiplexer #(.enable("false")) multiplexer_1 (
    .in0(output_o[0]), .in1(input_i[0]), .out(multiplexer_1_out), .sel(not_1_out));
  Multiplexer #(.enable("false")) multiplexer_2 (
    .in0(output_o[1]), .in1(input_i[1]), .out(multiplexer_2_out), .sel(not_1_out));
  Multiplexer #(.enable("false")) multiplexer_3 (
    .in0(output_o[2]), .in1(input_i[2]), .out(multiplexer_3_out), .sel(not_1_out));
  Multiplexer #(.enable("false")) multiplexer_4 (
    .in0(output_o[3]), .in1(input_i[3]), .out(multiplexer_4_out), .sel(not_1_out));
  Multiplexer #(.enable("false")) multiplexer_5 (
    .in0(output_o[4]), .in1(input_i[4]), .out(multiplexer_5_out), .sel(not_1_out));
  Multiplexer #(.enable("false")) multiplexer_6 (
    .in0(output_o[5]), .in1(input_i[5]), .out(multiplexer_6_out), .sel(not_1_out));
  Multiplexer #(.enable("false")) multiplexer_7 (
    .in0(output_o[6]), .in1(input_i[6]), .out(multiplexer_7_out), .sel(not_1_out));
  D_Flip_Flop d_ff_1 (.D(multiplexer_1_out), .clk(clk_i), .Q(output_o[0]), .preset(reset_i));  // open: Qn, reset
  D_Flip_Flop d_ff_2 (.D(multiplexer_2_out), .clk(clk_i), .Q(output_o[1]), .reset(reset_i));  // open: Qn, preset
  D_Flip_Flop d_ff_3 (.D(multiplexer_3_out), .clk(clk_i), .Q(output_o[2]), .reset(reset_i));  // open: Qn, preset
  D_Flip_Flop d_ff_4 (.D(multiplexer_4_out), .clk(clk_i), .Q(output_o[3]), .reset(reset_i));  // open: Qn, preset
  D_Flip_Flop d_ff_5 (.D(multiplexer_5_out), .clk(clk_i), .Q(output_o[4]), .reset(reset_i));  // open: Qn, preset
  D_Flip_Flop d_ff_6 (.D(multiplexer_6_out), .clk(clk_i), .Q(output_o[5]), .reset(reset_i));  // open: Qn, preset
  D_Flip_Flop d_ff_7 (.D(multiplexer_7_out), .clk(clk_i), .Q(output_o[6]), .reset(reset_i));  // open: Qn, preset

  // Notes on the sheet:
  //   Attention, votre version de Logisim
  //   ne contient pas de tracker. Si vous
  //   enregistrez votre projet, toutes les
  //   informations du tracker seront
  //   définitivement effacées.
endmodule

module compteur (
  input  load_i,
  input  en_i,
  input  clk_i,
  input  reset_i,
  output done_o
);

  wire [1:0] multiplexer_1_out, register_1_q, subtractor_1_out;

  Subtractor #(.width(2)) subtractor_1 (.a(register_1_q), .b(2'b01), .out(subtractor_1_out), .bin(1'b0));  // open: bout
  Multiplexer #(.width(2), .enable("false")) multiplexer_1 (
    .in0(subtractor_1_out), .in1(2'b11), .out(multiplexer_1_out), .sel(load_i));
  Register #(.width(2)) register_1 (.D(multiplexer_1_out), .en(en_i), .clk(clk_i), .Q(register_1_q), .clr(reset_i));
  Comparator #(.width(2)) comparator_1 (.a(register_1_q), .b(2'b01), .eq(done_o));  // open: gt, lt

  // Notes on the sheet:
  //   Attention, votre version de Logisim
  //   ne contient pas de tracker. Si vous
  //   enregistrez votre projet, toutes les
  //   informations du tracker seront
  //   définitivement effacées.
endmodule
