// Logisim project auto_arm_proj.circ as structural Verilog: 4 circuits, main circuit auto_arm_simulation
module auto_arm_simulation (
);

  wire auto_arm_top_1_dest_blue_o, auto_arm_top_1_dest_init_o, auto_arm_top_1_dest_red_o,
       auto_arm_top_1_drop_o, auto_arm_top_1_move_o, auto_arm_top_1_scan_o, auto_arm_top_1_throw_o,
       clk_i_out, tclconsolereds_1_p23, tclconsolereds_1_p26;
  wire [1:0] tclconsolereds_1_p24;

  Clock clk_i (.out(clk_i_out));
  Clock sysclk ();  // open: out
  auto_arm_top auto_arm_top_1 (
    .ready_i(tclconsolereds_1_p23), .color_i(tclconsolereds_1_p24), .clk_i(clk_i_out),
    .reset_i(tclconsolereds_1_p26), .scan_o(auto_arm_top_1_scan_o), .throw_o(auto_arm_top_1_throw_o),
    .move_o(auto_arm_top_1_move_o), .dest_red_o(auto_arm_top_1_dest_red_o),
    .dest_blue_o(auto_arm_top_1_dest_blue_o), .dest_init_o(auto_arm_top_1_dest_init_o),
    .drop_o(auto_arm_top_1_drop_o));
  // TclConsoleReds #(.filePath("console\\console_auto_arm.tcl")) tclconsolereds_1: pin names not known; wires that end beside it: 4'b0000, 4'b0000, auto_arm_top_1_scan_o, auto_arm_top_1_throw_o, auto_arm_top_1_move_o, auto_arm_top_1_dest_red_o, auto_arm_top_1_dest_blue_o, auto_arm_top_1_dest_init_o, auto_arm_top_1_drop_o, 1'b0, 1'b0, 1'b0, 1'b0, 1'b0, 1'b0, 1'b0, 1'b0, 1'b0, {16{1'b0}}, {16{1'b0}}, {8{1'b0}}, clk_i_out, tclconsolereds_1_p23, tclconsolereds_1_p24[0], tclconsolereds_1_p24[1], tclconsolereds_1_p26

  // Notes on the sheet:
  //   Attention, votre version de Logisim
  //   ne contient pas de tracker. Si vous
  //   enregistrez votre projet, toutes les
  //   informations du tracker seront
  //   définitivement effacées.
endmodule

module auto_arm_top (
  input  ready_i,
  input  [1:0] color_i,
  input  clk_i,
  input  reset_i,
  output scan_o,
  output throw_o,
  output move_o,
  output dest_red_o,
  output dest_blue_o,
  output dest_init_o,
  output drop_o
);

  wire [6:0] decodeur_d_etats_futurs_1_etat_futur, register_1_q;

  Decodeur_d_etats_futurs decodeur_d_etats_futurs_1 (
    .etat_present(register_1_q), .ready_i(ready_i), .color_i(color_i), .clk_i(clk_i),
    .etat_futur(decodeur_d_etats_futurs_1_etat_futur));
  Register #(.width(7)) register_1 (
    .D(decodeur_d_etats_futurs_1_etat_futur), .clk(clk_i), .Q(register_1_q), .clr(reset_i));  // open: en
  Decodeur_de_sorties decodeur_de_sorties_1 (
    .input_i(register_1_q), .output_o({scan_o, throw_o, move_o, dest_red_o, dest_blue_o, dest_init_o, drop_o}));

  // Notes on the sheet:
  //   Attention, votre version de Logisim
  //   ne contient pas de tracker. Si vous
  //   enregistrez votre projet, toutes les
  //   informations du tracker seront
  //   définitivement effacées.
endmodule

module Decodeur_de_sorties (
  input  [6:0] input_i,
  output [6:0] output_o
);

  wire [6:0] multiplexer_1_out, multiplexer_2_out;

  Multiplexer #(.select(4), .width(7), .enable("false")) multiplexer_1 (
    .in0({7{1'b0}}), .in1({7{1'b0}}), .in2(7'b1000000), .in4(7'b0100000), .in8(7'b0010100),
    .out(multiplexer_1_out), .sel(input_i[3:0]));  // open: in3, in5, in6, in7, in9, in10, in11, in12, in13, in14, in15
  Multiplexer #(.select(3), .width(7), .enable("false")) multiplexer_2 (
    .in0({7{1'b0}}), .in1(7'b0011000), .in2(7'b0000001), .in4(7'b0010010), .out(multiplexer_2_out),
    .sel(input_i[6:4]));  // open: in3, in5, in6, in7
  assign output_o = multiplexer_1_out | multiplexer_2_out;  // OR_Gate or_1, 7 bits wide

  // Notes on the sheet:
  //   Attention, votre version de Logisim
  //   ne contient pas de tracker. Si vous
  //   enregistrez votre projet, toutes les
  //   informations du tracker seront
  //   définitivement effacées.
endmodule

module Decodeur_d_etats_futurs (
  input  [6:0] etat_present,
  input  ready_i,
  input  [1:0] color_i,
  input  clk_i,
  output [6:0] etat_futur
);

  wire and_1_out, and_2_out, and_3_out, and_4_out, and_5_out, and_6_out, and_7_out, and_8_out, and_10_out,
       and_11_out, and_12_out, cpmtDone, xnor_1_out;

  and and_1 (and_1_out, etat_present[1], color_i[0], ~color_i[1]);  // AND_Gate
  or or_1 (etat_futur[3], and_1_out, and_2_out);
  and and_2 (and_2_out, etat_present[3], ~cpmtDone);  // AND_Gate
  NotExactlyOne xnor_1 (.out(xnor_1_out), .in0(etat_present[4]), .in1(etat_present[6]), .in2(etat_present[3]));
  Counter #(.width(2), .max('h3)) counter_1 (
    .load(xnor_1_out), .up(1'b0), .clk(clk_i), .D(2'b10), .carry(cpmtDone));  // open: clr, count, Q
  and and_3 (and_3_out, etat_present[1], ~color_i[0], color_i[1]);  // AND_Gate
  or or_2 (etat_futur[4], and_3_out, and_4_out);
  and and_4 (and_4_out, etat_present[4], ~cpmtDone);  // AND_Gate
  and and_5 (and_5_out, etat_present[0], ~ready_i);  // AND_Gate
  or or_3 (etat_futur[0], and_5_out, etat_present[2], and_6_out);
  and and_6 (and_6_out, etat_present[6], cpmtDone);
  and and_7 (and_7_out, etat_present[0], ready_i);
  or or_4 (etat_futur[1], and_7_out, and_8_out);
  and and_8 (and_8_out, etat_present[1], color_i[0], color_i[1]);
  and and_9 (etat_futur[2], etat_present[1], ~color_i[0], ~color_i[1]);  // AND_Gate
  and and_10 (and_10_out, etat_present[4], cpmtDone);
  and and_11 (and_11_out, etat_present[3], cpmtDone);
  or or_5 (etat_futur[5], and_10_out, and_11_out);
  and and_12 (and_12_out, etat_present[6], ~cpmtDone);  // AND_Gate
  or or_6 (etat_futur[6], etat_present[5], and_12_out);

  // Other names for the same wires on the sheet: color1 = color_i[0]; color2 = color_i[1]; idleNext = etat_futur[0];
  //   scanNext = etat_futur[1]; throwNext = etat_futur[2]; moveBlueNext = etat_futur[3]; moveRedNext = etat_futur[4];
  //   dropNext = etat_futur[5]; moveInitNext = etat_futur[6]; idle = etat_present[0]; scan = etat_present[1];
  //   throw = etat_present[2]; moveBlue = etat_present[3]; moveRed = etat_present[4]; drop = etat_present[5];
  //   moveInit = etat_present[6]; ready = ready_i

  // Notes on the sheet:
  //   Attention, votre version de Logisim
  //   ne contient pas de tracker. Si vous
  //   enregistrez votre projet, toutes les
  //   informations du tracker seront
  //   définitivement effacées.
endmodule
